// Logisim project FBU-CPU.circ as structural Verilog: 1 circuit, main circuit main
module main (
);

  wire Clk, comparator_1_eq, comparator_2_eq, comparator_2_lt, comparator_3_eq, comparator_4_eq,
       comparator_5_eq, comparator_6_eq, comparator_7_eq, comparator_8_eq, comparator_9_eq, comparator_10_eq,
       comparator_11_eq, multiplexer_7_out, RAMWrNext3, Rst;
  wire [2:0] durum, durumNext0, durumNext1, durumNext2, multiplexer_1_out, multiplexer_15_out,
       multiplexer_16_out, multiplexer_18_out, multiplexer_19_out;
  wire [5:0] MAR, MARNext0, MARNext1, MARNext3, multiplexer_2_out, multiplexer_5_out, multiplexer_6_out,
       multiplexer_9_out, pcNext1, pcNext2;
  wire [9:0] ACC, ACCNext3, adder_1_out, divider_1_out, IR, IRNext1, MDRIn, MDRInNext3, multiplexer_3_out,
       multiplexer_4_out, multiplexer_14_out, multiplexer_17_out, multiplexer_21_out, multiplexer_23_out,
       multiplexer_24_out, multiplier_1_out, subtractor_1_out;

  Button Reset (.out(Rst));
  Clock SaatClk (.out(Clk));
  Multiplexer #(.select(3), .width(3), .enable("false")) multiplexer_1 (
    .in0(durumNext0), .in1(durumNext1), .in2(durumNext2), .in3(3'b000), .in4(durum), .in5(3'b000),
    .in6(3'b000), .in7(3'b000), .out(multiplexer_1_out), .sel(durum));
  Multiplexer #(.select(3), .width(6), .enable("false")) multiplexer_2 (
    .in0(MARNext0), .in1(pcNext1), .in2(pcNext2), .in3(MARNext0), .in4(MARNext0), .in5({6{1'b0}}),
    .in6({6{1'b0}}), .in7({6{1'b0}}), .out(multiplexer_2_out), .sel(durum));
  Multiplexer #(.select(3), .width(10), .enable("false")) multiplexer_3 (
    .in0(IR), .in1(IRNext1), .in2(IR), .in3(IR), .in4(IR), .in5({10{1'b0}}), .in6({10{1'b0}}),
    .in7({10{1'b0}}), .out(multiplexer_3_out), .sel(durum));
  Multiplexer #(.select(3), .width(10), .enable("false")) multiplexer_4 (
    .in0(ACC), .in1(ACC), .in2(ACC), .in3(ACCNext3), .in4(ACC), .in5({10{1'b0}}), .in6({10{1'b0}}),
    .in7({10{1'b0}}), .out(multiplexer_4_out), .sel(durum));
  Register #(.width(3)) register_1 (.D(multiplexer_1_out), .en(1'b1), .clk(Clk), .Q(durum), .clr(Rst));
  Register #(.width(6)) register_2 (.D(multiplexer_2_out), .en(1'b1), .clk(Clk), .Q(MARNext0), .clr(Rst));
  Register #(.width(10)) register_3 (.D(multiplexer_3_out), .en(1'b1), .clk(Clk), .Q(IR), .clr(Rst));
  Register #(.width(10)) register_4 (.D(multiplexer_4_out), .en(1'b1), .clk(Clk), .Q(ACC), .clr(Rst));
  Multiplexer #(.width(6), .enable("false")) multiplexer_5 (
    .in0(MARNext0), .in1(IR[5:0]), .out(multiplexer_5_out), .sel(comparator_1_eq));
  Comparator #(.width(10), .mode("unsigned")) comparator_1 (
    .a(ACC), .b({10{1'b0}}), .eq(comparator_1_eq));  // open: gt, lt
  Comparator #(.width(4), .mode("unsigned")) comparator_2 (
    .a(IR[9:6]), .b(4'b0110), .eq(comparator_2_eq), .lt(comparator_2_lt));  // open: gt
  Comparator #(.width(4), .mode("unsigned")) comparator_3 (
    .a(IR[9:6]), .b(4'b0111), .eq(comparator_3_eq));  // open: gt, lt
  Comparator #(.width(4), .mode("unsigned")) comparator_4 (
    .a(IR[9:6]), .b(4'b1000), .eq(comparator_4_eq));  // open: gt, lt
  Comparator #(.width(4), .mode("unsigned")) comparator_5 (
    .a(IR[9:6]), .b(4'b1001), .eq(comparator_5_eq));  // open: gt, lt
  Comparator #(.width(4)) comparator_6 (.a(IR[9:6]), .b(4'b0000), .eq(comparator_6_eq));  // open: gt, lt
  Comparator #(.width(4)) comparator_7 (.a(IR[9:6]), .b(4'b0001), .eq(comparator_7_eq));  // open: gt, lt
  Comparator #(.width(4)) comparator_8 (.a(IR[9:6]), .b(4'b0010), .eq(comparator_8_eq));  // open: gt, lt
  Comparator #(.width(4)) comparator_9 (.a(IR[9:6]), .b(4'b0011), .eq(comparator_9_eq));  // open: gt, lt
  Comparator #(.width(4)) comparator_10 (.a(IR[9:6]), .b(4'b0100), .eq(comparator_10_eq));  // open: gt, lt
  Comparator #(.width(4)) comparator_11 (.a(IR[9:6]), .b(4'b0101), .eq(comparator_11_eq));  // open: gt, lt
  Multiplexer #(.select(3), .width(6), .enable("false")) multiplexer_6 (
    .in0(MARNext0), .in1(MARNext1), .in2(MAR), .in3(MARNext3), .in4({6{1'b0}}), .in5({6{1'b0}}),
    .in6({6{1'b0}}), .in7({6{1'b0}}), .out(multiplexer_6_out), .sel(durum));
  Multiplexer #(.select(3), .enable("false")) multiplexer_7 (
    .in0(1'b0), .in1(1'b0), .in2(1'b0), .in3(RAMWrNext3), .in4(1'b0), .in5(1'b0), .in6(1'b0), .in7(1'b0),
    .out(multiplexer_7_out), .sel(durum));
  Multiplexer #(.select(3), .width(10), .enable("false")) multiplexer_8 (
    .in0({10{1'b0}}), .in1({10{1'b0}}), .in2({10{1'b0}}), .in3(MDRInNext3), .in4({10{1'b0}}),
    .in5({10{1'b0}}), .in6({10{1'b0}}), .in7({10{1'b0}}), .out(MDRIn), .sel(durum));
  Multiplexer #(.width(6), .enable("false")) multiplexer_9 (
    .in0(MARNext0), .in1(multiplexer_5_out), .out(multiplexer_9_out), .sel(comparator_3_eq));
  Multiplexer #(.width(6), .enable("false")) multiplexer_10 (
    .in0(MAR), .in1(IR[5:0]), .out(MAR), .sel(comparator_2_lt));
  Multiplexer #(.width(6), .enable("false")) multiplexer_11 (
    .in0(MAR), .in1(IR[5:0]), .out(MARNext3), .sel(comparator_7_eq));
  Multiplexer #(.width(6), .enable("false")) multiplexer_12 (
    .in0(multiplexer_9_out), .in1(IR[5:0]), .out(pcNext2), .sel(comparator_2_eq));
  Multiplexer #(.enable("false")) multiplexer_13 (.in0(1'b0), .in1(1'b1), .out(RAMWrNext3), .sel(comparator_7_eq));
  RAM #(.addrWidth(6), .dataWidth(10), .databus("bibus")) RAM10Bit (
    .addr(multiplexer_6_out), .we(multiplexer_7_out), .oe(1'b1), .clk(Clk), .din(MDRIn), .dout(IRNext1));
  Multiplexer #(.width(10), .enable("false")) multiplexer_14 (
    .in0(ACC), .in1(IRNext1), .out(multiplexer_14_out), .sel(comparator_6_eq));
  Multiplexer #(.width(3), .enable("false")) multiplexer_15 (
    .in0(durum), .in1(3'b100), .out(multiplexer_15_out), .sel(comparator_5_eq));
  Multiplexer #(.width(3), .enable("false")) multiplexer_16 (
    .in0(multiplexer_15_out), .in1(3'b000), .out(multiplexer_16_out), .sel(comparator_4_eq));
  Multiplexer #(.width(10), .enable("false")) multiplexer_17 (
    .in0(multiplexer_14_out), .in1(ACC), .out(multiplexer_17_out), .sel(comparator_7_eq));
  Adder #(.width(10)) adder_1 (.a(ACC), .b(IRNext1), .out(adder_1_out));  // open: cin, cout
  Subtractor #(.width(10)) subtractor_1 (.a(ACC), .b(IRNext1), .out(subtractor_1_out));  // open: bin, bout
  Multiplier #(.width(10)) multiplier_1 (.a(ACC), .b(IRNext1), .out(multiplier_1_out));  // open: cin, cout
  Divider #(.width(10)) divider_1 (.a(ACC), .b(IRNext1), .out(divider_1_out));  // open: upper, rem
  Multiplexer #(.width(3), .enable("false")) multiplexer_18 (
    .in0(multiplexer_16_out), .in1(3'b000), .out(multiplexer_18_out), .sel(comparator_3_eq));
  Multiplexer #(.width(3), .enable("false")) multiplexer_19 (
    .in0(multiplexer_18_out), .in1(3'b000), .out(multiplexer_19_out), .sel(comparator_2_eq));
  Multiplexer #(.width(10), .enable("false")) multiplexer_20 (
    .in1(ACC), .out(MDRIn), .sel(comparator_7_eq));  // open: in0
  Multiplexer #(.width(10), .enable("false")) multiplexer_21 (
    .in0(multiplexer_17_out), .in1(adder_1_out), .out(multiplexer_21_out), .sel(comparator_8_eq));
  Multiplexer #(.width(3), .enable("false")) multiplexer_22 (
    .in0(multiplexer_19_out), .in1(3'b011), .out(durumNext2), .sel(comparator_2_lt));
  Multiplexer #(.width(10), .enable("false")) multiplexer_23 (
    .in0(multiplexer_21_out), .in1(subtractor_1_out), .out(multiplexer_23_out), .sel(comparator_9_eq));
  Multiplexer #(.width(10), .enable("false")) multiplexer_24 (
    .in0(multiplexer_23_out), .in1(multiplier_1_out), .out(multiplexer_24_out), .sel(comparator_10_eq));
  Multiplexer #(.width(10), .enable("false")) multiplexer_25 (
    .in0(multiplexer_24_out), .in1(divider_1_out), .out(ACCNext3), .sel(comparator_11_eq));
  Adder #(.width(3)) adder_2 (.a(durum), .b(3'b001), .out(durumNext0));  // open: cin, cout
  Adder #(.width(3)) adder_3 (.a(durum), .b(3'b001), .out(durumNext1));  // open: cin, cout
  Adder #(.width(6)) adder_4 (.a(MARNext0), .b(6'b000001), .out(pcNext1));  // open: cin, cout

  // Other names for the same wires on the sheet: ACCNext0[9:0] = ACC; ACCNext1[9:0] = ACC; ACCNext2[9:0] = ACC;
  //   ACCNext4[9:0] = ACC; durumNext4[2:0] = durum; IRNext0[9:0] = IR; IRNext2[9:0] = IR; IRNext3[9:0] = IR;
  //   IRNext4[9:0] = IR; MARNext2[5:0] = MAR; MDROut[9:0] = IRNext1; PC[5:0] = MARNext0; pcNext0[5:0] = MARNext0;
  //   pcNext3[5:0] = MARNext0; pcNext4[5:0] = MARNext0

  // Notes on the sheet:
  //   durum
  //   PC
  //   IR
  //   ACC
  //   durumNext
  //   PCNext
  //   IRNext
  //   ACCNext
  //   MAR
  //   RAMWr
  //   MDRIn
  //   durum0
  //   durum1
  //   durum2
  //   durum3
  //   durum4
  //   -----------------------------------------------------------------
  //   -----------------------------------------------------------------
  //   -----------------------------------------------------------------
  //   -----------------------------------------------------------------
  //   -----------------------------------------------------------------
  //   -----------------------------------------------------------------
  //   -----------------------------------------------------------------
  //   -----------------------------------------------------------------
  //   -----------------------------------------------------------------
  //   -----------------------------------------------------------------
  //   -----------------------------------------------------------------
endmodule
